# Fritzing sketch Manual_Control (saved by Fritzing 0.8.5b)

parts:
  Part1 = Arduino Uno (Rev3)
  U1 = POT [package=pot_alpha_rv16af-20]

nets:
  N1: Part1.A0, U1.E
  N2: Part1.A2, U1.S
  N3: Part1.A4/SDA, U1.A

notes:
  To PWM Control of ESC
  To GND of ESC
  *Wiring Note:
  just in case, plug in pot after your first upload
